# Fritzing sketch schema (saved by Fritzing 0.9.3b)

parts:
  Part3 = Arduino Uno (Rev3)
  Part5 = MCP9808
  Componente1 = Adafruit DS3231 [part_number="Adafruit #3013"]
  Componente2 = Adafruit RGB LCD Shield [part_number="Adafruit #714 and #716"]
  HLK-PM1 = HLK-PM01
  2_Channel_Relay1 = 2 Channel Power Relay
  L1 = Solenoid

nets:
  N1: Part3.A0, Componente2.A0
  N2: Part3.A1, Componente2.A1
  N3: Part3.A2, Componente2.A2
  N4: Part3.A3, Componente2.A3
  N5: Part3.A4/SDA, Part5.SDA, Componente1.SDA, Componente2.SDA
  N6: Part3.A5/SCL, Part5.SCL, Componente1.SCL, Componente2.SCL
  N7: Part3.D8, Componente2.D8
  N8: Part3.D9_PWM, Componente2.D9
  N9: Part3.D10_PWM/SS, Componente2.D10
  N10: Part3.D11_PWM/MOSI, Componente2.D11, 2_Channel_Relay1.IN1
  N11: Part3.D12/MISO, Componente2.D12
  N12: Part3.D13/SCK, Componente2.D13
  GND: Part3.GND, Part5.GND, Componente1.GND, Componente2.GND, HLK-PM1.-Vo, 2_Channel_Relay1.GND
  N13: Part3.AREF, Componente2.AREF
  N14: Part3.D0/RX, Componente2.D0
  N15: Part3.D1/TX, Componente2.D1
  N16: Part3.D2, Componente2.D2
  N17: Part3.D3_PWM, Componente2.D3
  N18: Part3.D4, Componente2.D4
  N19: Part3.D5_PWM, Componente2.D5
  N20: Part3.D6_PWM, Componente2.D6
  N21: Part3.D7, Componente2.D7
  N22: Part3.RESET, Componente2.RESET
  3V3: Part3.3V3, Componente2.3.3V
  5V: Part3.5V, Part5.VCC, Componente1.Vin, Componente2.+5V, HLK-PM1.+Vo, 2_Channel_Relay1.VCC#14
  VIN: Part3.VIN, Componente2.VIN
  N23: 2_Channel_Relay1.JD-VCC, 2_Channel_Relay1.VCC#9
  N24: 2_Channel_Relay1.K1-COM, L1.pin1
  N25: 2_Channel_Relay1.K1-NO, L1.pin2

notes:
  this is not the same supply but quite
  ELECTROVALVE
  under LCD there is Arduino

custom parts:
  Adafruit DS3231: The datasheet for the DS3231 explains that this part is an "Extremely Accurate I²C-Integrated RTC/TCXO/Crystal". And, hey, it does exactly what it says on the tin! This Real Time Clock (RTC) is the most precise you can get in a small, low power package. Most RTCs use an external 32kHz timing crystal that is used to keep time with low current draw. And that's all well and good, but those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
  Adafruit RGB LCD Shield: This new Adafruit shield makes it easy to use a 16x2 Character LCD. We really like the RGB LCDs we stock in the shop both the RGB negative and RGB positive. Unfortunately, these LCDs do require quite a few digital pins, 6 to control the LCD and then another 3 to control the RGB backlight for a total of 9 pins. That's half of the pins available on a classic Arduino! With this in mind, we wanted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
  2 Channel Power Relay: A 2 channel power relay. The module operates at 5V.
